# Fritzing sketch eMA1_fill (saved by Fritzing 0.6.5b)
breadboards: 1

parts:
  IC2 = L293N
  P1 = screw terminal, 4 pins
  D1 = Rectifier Diode [part_number=1N4001 package="300 mil [THT]"]
  D2 = Rectifier Diode [part_number=1N4001 package="300 mil [THT]"]
  D3 = Rectifier Diode [part_number=1N4001 package="300 mil [THT]"]
  D4 = Rectifier Diode [part_number=1N4001 package="300 mil [THT]"]
  D5 = Rectifier Diode [part_number=1N4001 package="300 mil [THT]"]
  D6 = Rectifier Diode [part_number=1N4001 package="300 mil [THT]"]
  D7 = Rectifier Diode [part_number=1N4001 package="300 mil [THT]"]
  D8 = Rectifier Diode [part_number=1N4001 package="300 mil [THT]"]
  P4 = female pin header, 4 pins [form="♀ (female)"]
  P3 = male pin header, 6 pins [form="♂ (male)"]
  C1 = Ceramic Capacitor [capacitance=100nF package="100 mil [THT, multilayer]"]
  IC1 = SOIC-14 [chip_label=IC spacing=300mil package=SO]
  J1 = shrouded pin header, 10 pins [form="♂ (shrouded male)"]

nets:
  GND: IC2.connector0, IC2.connector7, IC2.connector14, D5.anode, D6.anode, D7.anode, D8.anode, P4.pin2, P4.pin3, P3.pin3, C1.0, IC1.14, J1.pin2
  N1: IC2.connector1, P1.pin1, D1.anode, D5.cathode
  N2: IC2.connector2, P1.pin2, D2.anode, D6.cathode
  12V: IC2.connector3, D1.cathode, D2.cathode, D3.cathode, D4.cathode, P4.pin1
  N3: IC2.connector4, IC1.7
  N4: IC2.connector5, IC1.5
  N5: IC2.connector6, IC1.6
  5V: IC2.connector8, P4.pin4, P3.pin2, C1.1, IC1.1, J1.pin1
  N6: IC2.connector9, IC1.11
  N7: IC2.connector10, IC1.2
  N8: IC2.connector11, IC1.8
  N9: IC2.connector12, P1.pin3, D3.anode, D7.cathode
  N10: IC2.connector13, P1.pin4, D4.anode, D8.cathode
  N11: P3.pin1, IC1.4
  N12: P3.pin4, IC1.13
  N13: P3.pin5, IC1.12
  N14: IC1.3, J1.pin10
  N15: IC1.9, J1.pin7
  N16: IC1.10, J1.pin8

notes:
  eMA1 v1
  stepper motor control
