# Fritzing sketch eMH1 (saved by Fritzing 0.6.5b)
breadboards: 1

parts:
  P4 = female pin header, 4 pins [form="♀ (female)"]
  P2 = male pin header, 4 pins [form="♂ (male)"]  # not connected
  CONN1 = USB connector [package=THT]  # not connected
  Y1 = Resonator [frequency=0pMHz package=THT]  # not connected
  IC2 = SO08 [chip_label=IC spacing=300mil package=SO]  # not connected
  P1 = female pin header, 6 pins [form="♀ (female)"]  # not connected
  IC1 = SO20W [chip_label=IC spacing=300mil package=SO(w)]  # not connected

nets:
  12V: P4.pin1
  GND: P4.pin2, P4.pin3
  5V: P4.pin4
