# Fritzing sketch eM_base (saved by Fritzing 0.6.5b)
breadboards: 1

parts:
  P4 = female pin header, 4 pins [form="♀ (female)"]
  P2 = male pin header, 4 pins [form="♂ (male)"]  # not connected

nets:
  12V: P4.pin1
  GND: P4.pin2, P4.pin3
  5V: P4.pin4
